// Logisim project Cache.circ as structural Verilog: 4 circuits, main circuit Cache_Unit
module Cache_Unit (
  input  [31:0] Adress,
  input  [31:0] WriteData,
  input  MemRead,
  input  MemWrite,
  input  Clk,
  input  Reset,
  input  [3:0] WT,
  input  [3:0] RT,
  input  [31:0] RAM_O0,
  input  [31:0] RAM_O1,
  input  [31:0] RAM_O2,
  input  [31:0] RAM_O3,
  output [31:0] ReadData,
  output Stall,
  output To_CS,
  output To_RW,
  output [31:0] To_I0,
  output [31:0] To_I1,
  output [31:0] To_I2,
  output [31:0] To_I3
);

  wire cache_controller_1_cache_write, cache_system_1_hit;
  wire [13:0] Tag_Leido;

  Cache_System cache_system_1 (
    .Address(Adress), .Cache_Write(cache_controller_1_cache_write), .Clk(Clk), .RAM_O0(RAM_O0),
    .RAM_O1(RAM_O1), .RAM_O2(RAM_O2), .RAM_O3(RAM_O3), .CPU_ReadData(ReadData), .Tag_Leido(Tag_Leido),
    .Hit(cache_system_1_hit));  // open: Bit_V_Leido
  Cache_Controller cache_controller_1 (
    .Clk(Clk), .Reset(Reset), .Hit(cache_system_1_hit), .MemRead(MemRead), .MemWrite(MemWrite),
    .Stall(Stall), .Cache_Write(cache_controller_1_cache_write), .Ram_CS(To_CS), .Ram_RW(To_RW),
    .WriteTime(WT), .ReadTimme(RT));

  assign To_I0 = WriteData;
  assign To_I1 = WriteData;
  assign To_I2 = WriteData;
  assign To_I3 = WriteData;

  // Other names for the same wires on the sheet: Write_Data[31:0] = WriteData
endmodule

module Cache_Line (
  input  In_Valid,
  input  [13:0] In_Tag,
  input  [31:0] In_W0,
  input  [31:0] In_W1,
  input  [31:0] In_W2,
  input  [31:0] In_W3,
  input  Clk,
  input  Write_En,
  output out_9,
  output [13:0] out_10,
  output [31:0] out_11,
  output [31:0] out_12,
  output [31:0] out_13,
  output [31:0] out_14
);

  Register #(.width(1)) Valid (.D(In_Valid), .Q(out_9));  // open: en, clk, clr
  Register #(.width(14)) Tag (.D(In_Tag), .Q(out_10));  // open: en, clk, clr
  Register #(.width(32)) Word0 (.D(In_W0), .en(Write_En), .Q(out_11), .clk(Clk));  // open: clr
  Register #(.width(32)) Word1 (.D(In_W1), .en(Write_En), .Q(out_12), .clk(Clk));  // open: clr
  Register #(.width(32)) Word2 (.D(In_W2), .en(Write_En), .Q(out_13), .clk(Clk));  // open: clr
  Register #(.width(32)) Word3 (.D(In_W3), .en(Write_En), .Q(out_14), .clk(Clk));  // open: clr
endmodule

module Cache_System (
  input  [31:0] Address,
  input  Cache_Write,
  input  Clk,
  input  [31:0] RAM_O0,
  input  [31:0] RAM_O1,
  input  [31:0] RAM_O2,
  input  [31:0] RAM_O3,
  output [31:0] CPU_ReadData,
  output [13:0] Tag_Leido,
  output Hit,
  output Bit_V_Leido
);

  wire cache_line_1_out_9, cache_line_2_out_9, cache_line_3_out_9, cache_line_4_out_9, comparator_1_eq,
       decoder_1_out0, decoder_1_out1, decoder_1_out2, decoder_1_out3, Write_En_0, Write_En_1, Write_En_2,
       Write_En_3;
  wire [13:0] cache_line_1_out_10, cache_line_2_out_10, cache_line_3_out_10, cache_line_4_out_10;
  wire [31:0] multiplexer_3_out, multiplexer_4_out, multiplexer_5_out, multiplexer_6_out, Out_W0_0, Out_W0_1,
       Out_W0_2, Out_W0_3, Out_W1_0, Out_W1_1, Out_W1_2, Out_W1_3, Out_W2_0, Out_W2_1, Out_W2_2, Out_W2_3,
       Out_W3_0, Out_W3_1, Out_W3_2, Out_W3_3;

  Cache_Line cache_line_1 (
    .In_Valid(1'b1), .In_Tag(Address[19:6]), .Clk(Clk), .Write_En(Write_En_0), .out_9(cache_line_1_out_9),
    .out_10(cache_line_1_out_10), .out_11(Out_W0_0), .out_12(Out_W1_0), .out_13(Out_W2_0), .out_14(Out_W3_0),
    .In_W0(RAM_O0), .In_W1(RAM_O1), .In_W2(RAM_O2), .In_W3(RAM_O3));
  Cache_Line cache_line_2 (
    .In_Valid(1'b1), .In_Tag(Address[19:6]), .Clk(Clk), .Write_En(Write_En_1), .out_9(cache_line_2_out_9),
    .out_10(cache_line_2_out_10), .out_11(Out_W0_1), .out_12(Out_W1_1), .out_13(Out_W2_1), .out_14(Out_W3_1),
    .In_W0(RAM_O0), .In_W1(RAM_O1), .In_W2(RAM_O2), .In_W3(RAM_O3));
  Cache_Line cache_line_3 (
    .In_Valid(1'b1), .In_Tag(Address[19:6]), .Clk(Clk), .Write_En(Write_En_2), .out_9(cache_line_3_out_9),
    .out_10(cache_line_3_out_10), .out_11(Out_W0_2), .out_12(Out_W1_2), .out_13(Out_W2_2), .out_14(Out_W3_2),
    .In_W0(RAM_O0), .In_W1(RAM_O1), .In_W2(RAM_O2), .In_W3(RAM_O3));
  Cache_Line cache_line_4 (
    .In_Valid(1'b1), .In_Tag(Address[19:6]), .Clk(Clk), .Write_En(Write_En_3), .out_9(cache_line_4_out_9),
    .out_10(cache_line_4_out_10), .out_11(Out_W0_3), .out_12(Out_W1_3), .out_13(Out_W2_3), .out_14(Out_W3_3),
    .In_W0(RAM_O0), .In_W1(RAM_O1), .In_W2(RAM_O2), .In_W3(RAM_O3));
  Decoder #(.select(2)) decoder_1 (
    .out0(decoder_1_out0), .out1(decoder_1_out1), .out2(decoder_1_out2), .out3(decoder_1_out3),
    .sel(Address[5:4]));  // open: en
  Multiplexer #(.select(2), .width(14)) multiplexer_1 (
    .in0(cache_line_1_out_10), .in1(cache_line_2_out_10), .in2(cache_line_3_out_10),
    .in3(cache_line_4_out_10), .out(Tag_Leido), .sel(Address[5:4]));  // open: en
  Multiplexer #(.select(2)) multiplexer_2 (
    .in0(cache_line_1_out_9), .in1(cache_line_2_out_9), .in2(cache_line_3_out_9), .in3(cache_line_4_out_9),
    .out(Bit_V_Leido), .sel(Address[5:4]));  // open: en
  Comparator #(.width(14)) comparator_1 (.a(Address[19:6]), .b(Tag_Leido), .eq(comparator_1_eq));  // open: gt, lt
  and and_1 (Write_En_0, decoder_1_out0, Cache_Write);
  and and_2 (Write_En_1, decoder_1_out1, Cache_Write);
  and and_3 (Write_En_2, decoder_1_out2, Cache_Write);
  and and_4 (Write_En_3, decoder_1_out3, Cache_Write);
  and and_5 (Hit, comparator_1_eq, Bit_V_Leido);
  Multiplexer #(.select(2), .width(32)) multiplexer_3 (
    .in0(Out_W0_0), .in1(Out_W0_1), .in2(Out_W0_2), .in3(Out_W0_3), .out(multiplexer_3_out),
    .sel(Address[5:4]));  // open: en
  Multiplexer #(.select(2), .width(32)) multiplexer_4 (
    .in0(Out_W1_0), .in1(Out_W1_1), .in2(Out_W1_2), .in3(Out_W1_3), .out(multiplexer_4_out),
    .sel(Address[5:4]));  // open: en
  Multiplexer #(.select(2), .width(32)) multiplexer_5 (
    .in0(Out_W2_0), .in1(Out_W2_1), .in2(Out_W2_2), .in3(Out_W2_3), .out(multiplexer_5_out),
    .sel(Address[5:4]));  // open: en
  Multiplexer #(.select(2), .width(32)) multiplexer_6 (
    .in0(Out_W3_0), .in1(Out_W3_1), .in2(Out_W3_2), .in3(Out_W3_3), .out(multiplexer_6_out),
    .sel(Address[5:4]));  // open: en
  Multiplexer #(.select(2), .width(32)) multiplexer_7 (
    .in0(multiplexer_3_out), .in1(multiplexer_4_out), .in2(multiplexer_5_out), .in3(multiplexer_6_out),
    .out({CPU_ReadData[7:0], CPU_ReadData[15:8], CPU_ReadData[23:16], CPU_ReadData[31:24]}),
    .sel(Address[3:2]));  // open: en

  // Other names for the same wires on the sheet: Word_Sel[1:0] = Address[3:2]; Index[1:0] = Address[5:4];
  //   Tag[13:0] = Address[19:6]
endmodule

module Cache_Controller (
  input  Clk,
  input  Reset,
  input  Hit,
  input  MemRead,
  input  MemWrite,
  input  [3:0] ReadTimme,
  input  [3:0] WriteTime,
  output Stall,
  output Cache_Write,
  output Ram_CS,
  output Ram_RW
);

  wire and_2_out, and_3_out, comparator_1_gt, comparator_2_eq, Load, MRW, or_2_out, or_3_out, RAM_Done;
  wire [0:0] and_1_out;
  wire [1:0] multiplexer_1_out, multiplexer_3_out;
  wire [1:1] Current_State;
  wire [3:0] counter_1_q, multiplexer_4_out, register_1_q, subtractor_1_out, TargetMemory;

  Multiplexer #(.width(2), .enable("false")) multiplexer_1 (
    .in0(2'b01), .in1(2'b10), .out(multiplexer_1_out), .sel(RAM_Done));
  or or_1 (MRW, MemRead, MemWrite);
  // Probe on {Current_State[1], Ram_CS}
  Register #(.width(2)) u_Current_State (
    .D(multiplexer_3_out), .en(1'b1), .Q({Current_State[1], Ram_CS}), .clk(Clk), .clr(Reset));
  and and_1 (and_1_out[0], ~Hit, MRW);  // AND_Gate
  or or_2 (or_2_out, Ram_CS, Current_State[1]);
  Multiplexer #(.width(4), .enable("false")) multiplexer_2 (
    .in0(ReadTimme), .in1(WriteTime), .out(TargetMemory), .sel(MemWrite));
  // Probe on TargetMemory
  Multiplexer #(.select(2), .width(2)) multiplexer_3 (
    .in0({1'b0, and_1_out[0]}), .in1(multiplexer_1_out), .in2(2'b00), .in3(2'b00), .out(multiplexer_3_out),
    .sel({Current_State[1], Ram_CS}));  // open: en
  // Probe on multiplexer_3_out
  // Probe on TargetMemory
  Comparator #(.width(4)) comparator_1 (
    .a(register_1_q), .b(4'b0000), .gt(comparator_1_gt), .eq(RAM_Done));  // open: lt
  and and_2 (and_2_out, RAM_Done, or_2_out);
  and and_3 (and_3_out, Ram_CS, ~Current_State[1]);  // AND_Gate
  // Probe on subtractor_1_out
  D_Flip_Flop d_ff_1 (.clk(Clk), .D(and_2_out), .Q(Stall));  // open: Qn, preset, en, reset
  and and_4 (Cache_Write, RAM_Done, Ram_CS);
  and and_5 (Load, ~Ram_CS, ~Current_State[1], ~Hit, MRW);  // AND_Gate
  Counter #(.width(4), .max('hf), .ongoal("stay"), .trigger("falling")) counter_1 (
    .load(Load), .D(TargetMemory), .count(and_3_out), .Q(counter_1_q), .clk(Clk), .clr(Reset));  // open: carry
  // Probe on multiplexer_4_out
  Multiplexer #(.width(4), .enable("false")) multiplexer_4 (
    .in0(subtractor_1_out), .in1(TargetMemory), .out(multiplexer_4_out), .sel(Load));
  or or_3 (or_3_out, Load, comparator_1_gt);
  // Probe on counter_1_q
  Register #(.width(4)) register_1 (.D(multiplexer_4_out), .en(or_3_out), .Q(register_1_q), .clk(Clk), .clr(Reset));
  Comparator #(.width(4)) comparator_2 (.a(counter_1_q), .b(4'b0000), .eq(comparator_2_eq));  // open: gt, lt
  // Probe on register_1_q
  Subtractor #(.width(4)) subtractor_1 (.a(register_1_q), .b(4'b0001), .out(subtractor_1_out));  // open: bin, bout

  assign Ram_RW = MemWrite;

  // Other names for the same wires on the sheet: _0 = Reset; Current_State[0] = Ram_CS
endmodule
