// Logisim project ALU Controler.circ as structural Verilog: 2 circuits, main circuit main
module main (
  input  in_1,
  input  [2:0] ALUop,
  input  [5:0] FuncCode,
  output [3:0] out_4
);

  wire [3:0] multiplexer_1_out, tipo_r_coder_1_a4_2;

  Tipo_R_coder tipo_r_coder_1 (
    .a(FuncCode[5]), .a2(FuncCode[4]), .a3(FuncCode[3]), .a4(FuncCode[2]), .a5(FuncCode[1]),
    .a6(FuncCode[0]), .a_2(tipo_r_coder_1_a4_2[3]), .a2_2(tipo_r_coder_1_a4_2[2]),
    .a3_2(tipo_r_coder_1_a4_2[1]), .a4_2(tipo_r_coder_1_a4_2[0]));
  Multiplexer #(.width(4), .enable("false")) multiplexer_1 (
    .in0(4'b1001), .in1(4'b1011), .out(multiplexer_1_out), .sel(in_1));
  Multiplexer #(.select(3), .width(4), .enable("false")) multiplexer_2 (
    .in0(4'b0000), .in1(tipo_r_coder_1_a4_2), .in2(4'b0001), .in3(4'b0100), .in4(4'b0110), .in5(4'b1000),
    .in6(multiplexer_1_out), .in7(4'b1010), .out(out_4), .sel(ALUop));

  // Other names for the same wires on the sheet: SltiSign = in_1
endmodule

module Tipo_R_coder (
  input  a,
  input  a2,
  input  a3,
  input  a4,
  input  a5,
  input  a6,
  output a_2,
  output a2_2,
  output a3_2,
  output a4_2
);

  wire and_1_out, not_1_out, not_2_out;

  or or_1 (a2_2, a4, a2);
  not not_1 (not_1_out, a);
  not not_2 (not_2_out, a3);
  and and_1 (and_1_out, not_1_out, not_2_out);
  or or_2 (a3_2, and_1_out, a6);

  assign a4_2 = a5;
  assign a_2 = a3;
endmodule
