// Logisim project DataPath.circ as structural Verilog: 1 circuit, main circuit main
module main (
  input  in_1,
  input  in_2,
  input  in_3,
  input  [1:0] in_4,
  input  [1:0] in_5,
  input  in_6,
  input  in_7,
  input  in_8,
  input  in_9,
  input  [1:0] in_10,
  input  [3:0] in_11,
  input  [1:0] in_12,
  input  in_13,
  input  [6:0] KBDInput,
  input  in_15,
  input  in_16,
  input  in_17,
  input  in_18,
  input  in_19,
  input  in_20,
  output [6:0] TTY_Output,
  output [5:0] OpCode,
  output [5:0] FuncCode,
  output out_24,
  output out_25
);

  wire and_1_out, or_1_out;
  wire [4:0] multiplexer_3_out, multiplexer_4_out, multiplexer_5_out;
  wire [25:6] Instr_q;
  wire [27:0] shifter_2_out;
  wire [31:0] A_q, ALUOut_q, B_q, bit_extender_1_out, bit_extender_2_out, bit_extender_3_out, Data_q, Hi,
       KbdIn, Lo, main_2_rd, main_3_b, multiplexer_1_out, multiplexer_6_out, multiplexer_7_out,
       multiplexer_8_out, multiplexer_9_out, multiplexer_10_out, PC, shifter_1_out;
  wire [31:7] main_3_a;

  PC_main main_1 (.Input(multiplexer_10_out), .Enable(or_1_out), .Clk(in_1), .Output(PC), .Reset(in_20));
  Multiplexer #(.width(32)) multiplexer_1 (.in0(PC), .in1(ALUOut_q), .out(multiplexer_1_out), .sel(in_3));  // open: en
  inst_dataMemory_main main_2 (
    .WE(in_8), .Clock(in_1), .Instruction(multiplexer_1_out), .Write_Data(B_q), .RD(main_2_rd));
  Register #(.width(32)) Instr (.D(main_2_rd), .en(in_6), .Q({OpCode, Instr_q, FuncCode}), .clk(in_1), .clr(in_20));
  Register #(.width(32)) Data (.D(main_2_rd), .Q(Data_q), .clk(in_1), .clr(in_20));  // open: en
  assign bit_extender_1_out = {{25{KBDInput[6]}}, KBDInput};  // Bit_Extender bit_extender_1
  Multiplexer #(.width(32), .enable("false")) multiplexer_2 (
    .in0({32{1'b1}}), .in1(bit_extender_1_out), .out(KbdIn), .sel(in_16));
  Multiplexer #(.select(2), .width(5)) multiplexer_3 (
    .in0(Instr_q[20:16]), .in1(Instr_q[15:11]), .in2({5{1'b1}}), .out(multiplexer_3_out), .sel(in_10));  // open: in3, en
  Multiplexer #(.width(5), .enable("false")) multiplexer_4 (
    .in0(Instr_q[25:21]), .in1({5{1'b1}}), .out(multiplexer_4_out), .sel(in_17));
  Multiplexer #(.width(5), .enable("false")) multiplexer_5 (
    .in0(Instr_q[20:16]), .in1(Instr_q[25:21]), .out(multiplexer_5_out), .sel(in_18));
  Multiplexer #(.select(2), .width(32)) multiplexer_6 (
    .in0(Data_q), .in1(ALUOut_q), .in2(KbdIn), .out(multiplexer_6_out), .sel(in_12));  // open: in3, en
  Register_File_main main_3 (
    .Data_Input(multiplexer_6_out), .reset(in_20), .R_W(in_13), .clock(in_1), .SOp(in_17),
    .Data_Address(multiplexer_3_out), .Selector_A(multiplexer_4_out), .Selector_B(multiplexer_5_out),
    .High_in(Hi), .Low_in(Lo), .Hi_Lo_enable(in_19), .A({main_3_a, TTY_Output}), .B(main_3_b));  // open: PC_enable, Stack_Pointer, High_Out, Low_Out
  assign bit_extender_2_out = {{16{1'b0}}, {Instr_q[15:6], FuncCode}};  // Bit_Extender bit_extender_2
  assign bit_extender_3_out = {{16{Instr_q[15]}}, {Instr_q[15:6], FuncCode}};  // Bit_Extender bit_extender_3
  Register #(.width(32)) A (.D({main_3_a, TTY_Output}), .Q(A_q), .clk(in_1), .clr(in_20));  // open: en
  Register #(.width(32)) B (.D(main_3_b), .Q(B_q), .clk(in_1), .clr(in_20));  // open: en
  Multiplexer #(.width(32)) multiplexer_7 (
    .in0(bit_extender_3_out), .in1(bit_extender_2_out), .out(multiplexer_7_out), .sel(in_15));  // open: en
  Shifter #(.width(32)) shifter_1 (.in(bit_extender_3_out), .\dist (5'b00010), .out(shifter_1_out));
  Multiplexer #(.width(32)) multiplexer_8 (.in0(PC), .in1(A_q), .out(multiplexer_8_out), .sel(in_2));  // open: en
  Multiplexer #(.select(2), .width(32), .enable("false")) multiplexer_9 (
    .in0(B_q), .in1(32'h4), .in2(multiplexer_7_out), .in3(shifter_1_out), .out(multiplexer_9_out), .sel(in_4));
  Shifter #(.width(28)) shifter_2 (.in({OpCode[1:0], Instr_q, FuncCode}), .\dist (5'b00010), .out(shifter_2_out));
  ALU alu_1 (
    .in_1(multiplexer_8_out), .in_2(multiplexer_9_out), .in_3(in_11), .Result(Lo), .Helper_Result(Hi),
    .Zero_Flag(out_24), .Sign(out_25));  // open: Equal
  and and_1 (and_1_out, in_7, out_24);
  Register #(.width(32)) ALUOut (.D(Lo), .Q(ALUOut_q), .clk(in_1), .clr(in_20));  // open: en
  or or_1 (or_1_out, in_9, and_1_out);
  Multiplexer #(.select(2), .width(32), .enable("false")) multiplexer_10 (
    .in0(Lo), .in1(ALUOut_q), .in2({PC[31:28], shifter_2_out}), .out(multiplexer_10_out), .sel(in_5));  // open: in3

  // Other names for the same wires on the sheet: ALUControl[3:0] = in_11; ALUSrcA = in_2; ALUSrcB[1:0] = in_4;
  //   Branch = in_7; Clk = in_1; HiLoEn = in_19; IorD = in_3; IRWrite = in_6; MemtoReg[1:0] = in_12; MemWrite = in_8;
  //   PCSrc[1:0] = in_5; PCWrite = in_9; R_W = in_13; RegDst[1:0] = in_10; _0 = in_20; Reset = in_20; Sign = out_25;
  //   StackOp = in_17; UseRsAsB = in_18; Z_S = in_15; Zero = out_24

  // Notes on the sheet:
  //   ALU+4
endmodule
